// Logisim project ex_a.circ as structural Verilog
module Ex1 (
  input  [7:0] _8_bit_input,
  output Out1,
  output [7:0] Out2
);

  and and_1 (Out1, _8_bit_input[0], _8_bit_input[7]);
  not not_1 (Out2[7], _8_bit_input[7]);

  assign Out2[6:0] = _8_bit_input[6:0];
endmodule

module rotr (
  input  [15:0] \input ,
  input  [3:0] shamt,
  output [15:0] \output 
);

  rotr_sub rotr_sub_1 (.\input (\input ), .shamt(shamt), .offset(4'b0000), .out_4(\output [0]));
  rotr_sub rotr_sub_2 (.\input (\input ), .shamt(shamt), .offset(4'b0001), .out_4(\output [1]));
  rotr_sub rotr_sub_3 (.\input (\input ), .shamt(shamt), .offset(4'b0010), .out_4(\output [2]));
  rotr_sub rotr_sub_4 (.\input (\input ), .shamt(shamt), .offset(4'b0011), .out_4(\output [3]));
  rotr_sub rotr_sub_5 (.\input (\input ), .shamt(shamt), .offset(4'b0100), .out_4(\output [4]));
  rotr_sub rotr_sub_6 (.\input (\input ), .shamt(shamt), .offset(4'b0101), .out_4(\output [5]));
  rotr_sub rotr_sub_7 (.\input (\input ), .shamt(shamt), .offset(4'b0110), .out_4(\output [6]));
  rotr_sub rotr_sub_8 (.\input (\input ), .shamt(shamt), .offset(4'b0111), .out_4(\output [7]));
  rotr_sub rotr_sub_9 (.\input (\input ), .shamt(shamt), .offset(4'b1000), .out_4(\output [8]));
  rotr_sub rotr_sub_10 (.\input (\input ), .shamt(shamt), .offset(4'b1001), .out_4(\output [9]));
  rotr_sub rotr_sub_11 (.\input (\input ), .shamt(shamt), .offset(4'b1010), .out_4(\output [10]));
  rotr_sub rotr_sub_12 (.\input (\input ), .shamt(shamt), .offset(4'b1011), .out_4(\output [11]));
  rotr_sub rotr_sub_13 (.\input (\input ), .shamt(shamt), .offset(4'b1100), .out_4(\output [12]));
  rotr_sub rotr_sub_14 (.\input (\input ), .shamt(shamt), .offset(4'b1101), .out_4(\output [13]));
  rotr_sub rotr_sub_15 (.\input (\input ), .shamt(shamt), .offset(4'b1110), .out_4(\output [14]));
  rotr_sub rotr_sub_16 (.\input (\input ), .shamt(shamt), .offset(4'b1111), .out_4(\output [15]));
endmodule

module rotr_sub (
  input  [15:0] \input ,
  input  [3:0] shamt,
  input  [3:0] offset,
  output out_4
);

  wire [3:0] adder_1_out;

  Multiplexer #(.select(4)) multiplexer_1 (
    .in0(\input [0]), .in1(\input [1]), .in2(\input [2]), .in3(\input [3]), .in4(\input [4]),
    .in5(\input [5]), .in6(\input [6]), .in7(\input [7]), .in8(\input [8]), .in9(\input [9]),
    .in10(\input [10]), .in11(\input [11]), .in12(\input [12]), .in13(\input [13]), .in14(\input [14]),
    .in15(\input [15]), .out(out_4), .sel(adder_1_out));  // open: en
  Adder #(.width(4)) adder_1 (.a(shamt), .b(offset), .out(adder_1_out));  // open: cin, cout
endmodule

module fib15 (
  input  [3:0] input__n,
  output [9:0] output__fib_n
);

  wire clock_1_out, \continue ;
  wire [3:0] counter_1_q;
  wire [9:0] adder_1_out, register_1_q;

  Counter #(.width(4), .max('hf)) counter_1 (
    .load(1'b0), .count(\continue ), .Q(counter_1_q), .clk(clock_1_out));  // open: D, carry, clr
  // Probe on input__n
  Comparator #(.width(4), .mode("unsigned")) comparator_1 (
    .a(input__n), .b(counter_1_q), .gt(\continue ));  // open: eq, lt
  Clock clock_1 (.out(clock_1_out));
  Register #(.width(10)) register_1 (
    .D(adder_1_out), .en(\continue ), .Q(register_1_q), .clk(clock_1_out));  // open: clr
  Adder #(.width(10)) adder_1 (.a(register_1_q), .b(output__fib_n), .out(adder_1_out));  // open: cin, cout
  Register #(.width(10)) register_2 (
    .D(register_1_q), .en(\continue ), .Q(output__fib_n), .clk(clock_1_out));  // open: clr
  // Probe on output__fib_n
endmodule
