// Logisim project alu.circ as structural Verilog: 7 circuits, main circuit main
module main (
  input  [15:0] X,
  input  [15:0] Y,
  input  [3:0] Switch__S,
  output Signed_Overflow,
  output [15:0] RESULT,
  output Equal
);

  wire multiplexer_2_out, or_1_out, overflow8, overflow16, xnor_1_out;
  wire [15:0] add_sub_result, addp8_subp8_result, or_and_result, shift_result, slt_result;

  add_sub add_sub (.X(X), .Y(Y), .add_sub(Switch__S[0]), .result(add_sub_result), .overflow(overflow16));
  xnor xnor_1 (xnor_1_out, Switch__S[0], Switch__S[1]);
  addp8_subp8 addp8_subp8 (.X(X), .Y(Y), .add_sub(Switch__S[0]), .result(addp8_subp8_result), .overflow(overflow8));
  shift shift (.X(X), .Y(Y), .left_right(xnor_1_out), .arithmetic(Switch__S[2]), .result(shift_result));
  slt slt (.X(X), .Y(Y), .result(slt_result));
  or_and or_and (.X(X), .Y(Y), .or_and(Switch__S[0]), .result(or_and_result));
  Multiplexer #(.select(4), .width(16)) multiplexer_1 (
    .in0(add_sub_result), .in1(add_sub_result), .in2(shift_result), .in3(shift_result), .in4(shift_result),
    .in5(slt_result), .in6(or_and_result), .in7(or_and_result), .in8(addp8_subp8_result),
    .in9(addp8_subp8_result), .out(RESULT), .sel(Switch__S));  // open: in10, in11, in12, in13, in14, in15, en
  Multiplexer multiplexer_2 (
    .in0(overflow16), .in1(overflow8), .out(multiplexer_2_out), .sel(Switch__S[3]));  // open: en
  or or_1 (or_1_out, Switch__S[1], Switch__S[2]);
  Multiplexer multiplexer_3 (.in0(multiplexer_2_out), .in1(1'b0), .out(Signed_Overflow), .sel(or_1_out));  // open: en
  Comparator #(.width(16)) comparator_1 (.a(X), .b(Y), .eq(Equal));  // open: gt, lt

  // Other names for the same wires on the sheet: inputX[15:0] = X; inputY[15:0] = Y; sel0 = Switch__S[0];
  //   select[3:0] = Switch__S; sel1 = Switch__S[1]; sel2 = Switch__S[2]; sel3 = Switch__S[3]

  // Notes on the sheet:
  //   INPUTS to your circuit
  //   INPUT to your circuit
  //   DON'T CHANGE THE INPUTS AND OUTPUTS! IF YOU DO SO, YOU NEED TO MAKE SURE THE PINS ARE IN THE RIGHT PLACES!
  //   OUTPUTS of your circuit
endmodule

module add_sub (
  input  [15:0] X,
  input  [15:0] Y,
  input  add_sub,
  output [15:0] result,
  output overflow
);

  wire signR, signX, signY;
  wire [15:0] multiplexer_1_out, not_1_out;

  BitSelector #(.width(16)) bitselector_1 (.in(X), .out(signX), .sel(4'b1111));
  BitSelector #(.width(16)) bitselector_2 (.in(Y), .out(signY), .sel(4'b1111));
  assign not_1_out = ~Y;  // NOT_Gate not_1, 16 bits wide
  Adder #(.width(16)) adder_1 (.a(X), .b(multiplexer_1_out), .out(result), .cin(add_sub));  // open: cout
  Multiplexer #(.width(16)) multiplexer_1 (
    .in0(Y), .in1(not_1_out), .out(multiplexer_1_out), .sel(add_sub));  // open: en
  BitSelector #(.width(16)) bitselector_3 (.in(result), .out(signR), .sel(4'b1111));
  overflow u_overflow (
    .sign_bit_X(signX), .sign_bit_Y(signY), .subtract(add_sub), .sign_bit_result(signR), .overflow(overflow));

  // Other names for the same wires on the sheet: subtract = add_sub
endmodule

module overflow (
  input  sign_bit_X,
  input  sign_bit_Y,
  input  subtract,
  input  sign_bit_result,
  output overflow
);

  wire and_1_out, and_2_out, not_1_out, not_2_out, xnor_1_out, xor_1_out;

  xnor xnor_1 (xnor_1_out, sign_bit_Y, subtract);
  xor xor_1 (xor_1_out, sign_bit_Y, subtract);
  not not_1 (not_1_out, sign_bit_X);
  and and_1 (and_1_out, not_1_out, sign_bit_result, xnor_1_out);
  and and_2 (and_2_out, sign_bit_X, xor_1_out, not_2_out);
  not not_2 (not_2_out, sign_bit_result);
  or or_1 (overflow, and_1_out, and_2_out);
endmodule

module addp8_subp8 (
  input  [15:0] X,
  input  [15:0] Y,
  input  add_sub,
  output [15:0] result,
  output overflow
);

  wire overflow_2_overflow, overflow_overflow, signRhigh, signRlow;
  wire [7:0] adder_1_out, adder_2_out, subtractor_1_out, subtractor_2_out;

  Adder adder_1 (.a(X[7:0]), .b(Y[7:0]), .out(adder_1_out));  // open: cin, cout
  Adder adder_2 (.a(X[15:8]), .b(Y[15:8]), .out(adder_2_out));  // open: cin, cout
  Subtractor subtractor_1 (.a(X[7:0]), .b(Y[7:0]), .out(subtractor_1_out));  // open: bin, bout
  Subtractor subtractor_2 (.a(X[15:8]), .b(Y[15:8]), .out(subtractor_2_out));  // open: bin, bout
  overflow u_overflow (
    .sign_bit_X(X[7]), .sign_bit_Y(Y[7]), .subtract(add_sub), .sign_bit_result(signRlow),
    .overflow(overflow_overflow));
  overflow overflow_2 (
    .sign_bit_X(X[15]), .sign_bit_Y(Y[15]), .subtract(add_sub), .sign_bit_result(signRhigh),
    .overflow(overflow_2_overflow));
  or or_1 (overflow, overflow_overflow, overflow_2_overflow);
  Multiplexer multiplexer_1 (
    .in0(adder_1_out[7]), .in1(subtractor_1_out[7]), .out(signRlow), .sel(add_sub));  // open: en
  Multiplexer multiplexer_2 (
    .in0(adder_2_out[7]), .in1(subtractor_2_out[7]), .out(signRhigh), .sel(add_sub));  // open: en
  Multiplexer #(.width(16)) multiplexer_3 (
    .in0({adder_2_out, adder_1_out}), .in1({subtractor_2_out, subtractor_1_out}), .out(result), .sel(add_sub));  // open: en

  // Other names for the same wires on the sheet: subtract = add_sub; Xhigh[7:0] = X[15:8]; signXhigh = X[15];
  //   Xlow[7:0] = X[7:0]; signXlow = X[7]; Yhigh[7:0] = Y[15:8]; signYhigh = Y[15]; Ylow[7:0] = Y[7:0];
  //   signYlow = Y[7]
endmodule

module shift (
  input  [15:0] X,
  input  [15:0] Y,
  input  left_right,
  input  arithmetic,
  output [15:0] result
);

  wire [3:0] bitselector_1_out;
  wire [15:0] shifter_1_out, shifter_2_out, shifter_3_out;

  BitSelector #(.width(16), .group(4)) bitselector_1 (.in(Y), .out(bitselector_1_out), .sel(2'b00));
  Shifter #(.width(16)) shifter_1 (.in(X), .\dist (bitselector_1_out), .out(shifter_1_out));
  Shifter #(.width(16), .shift("lr")) shifter_2 (.in(X), .\dist (bitselector_1_out), .out(shifter_2_out));
  Shifter #(.width(16), .shift("ar")) shifter_3 (.in(X), .\dist (bitselector_1_out), .out(shifter_3_out));
  Multiplexer #(.select(2), .width(16)) multiplexer_1 (
    .in0(shifter_1_out), .in1(shifter_1_out), .in2(shifter_2_out), .in3(shifter_3_out), .out(result),
    .sel({left_right, arithmetic}));  // open: en
endmodule

module or_and (
  input  [15:0] X,
  input  [15:0] Y,
  input  or_and,
  output [15:0] result
);

  wire [15:0] and_1_out, or_1_out;

  assign or_1_out = X | Y;  // OR_Gate or_1, 16 bits wide
  assign and_1_out = X & Y;  // AND_Gate and_1, 16 bits wide
  Multiplexer #(.width(16)) multiplexer_1 (.in0(or_1_out), .in1(and_1_out), .out(result), .sel(or_and));  // open: en
endmodule

module slt (
  input  [15:0] X,
  input  [15:0] Y,
  output [15:0] result
);

  wire comparator_1_lt;

  Comparator #(.width(16)) comparator_1 (.a(X), .b(Y), .lt(comparator_1_lt));  // open: gt, eq
  Multiplexer #(.width(16)) multiplexer_1 (
    .in0({16{1'b0}}), .in1(16'h1), .out(result), .sel(comparator_1_lt));  // open: en
endmodule
