// Logisim project cpu.circ as structural Verilog: 14 circuits, main circuit main
module main (
  input  [15:0] From_Instr_Mem,
  input  clk,
  output [15:0] r0,
  output [15:0] r1,
  output [15:0] r2,
  output [15:0] r3,
  output [15:0] Display_0,
  output [15:0] Display_1,
  output [15:0] To_Instr_Mem,
  output [15:0] Data_Mem_Data,
  output [15:0] Data_Mem_Addr,
  output Data_Mem_Write
);

  wire AluEqual, AluOverflow, CntrlAnd_addi, CntrlAnd_andi, CntrlAnd_beq, CntrlAnd_bne, CntrlAnd_disp,
       CntrlAnd_j, CntrlAnd_jal, CntrlAnd_jr, CntrlAnd_lui, CntrlAnd_lw, CntrlAnd_ori, CntrlAnd_rtype,
       CntrlAnd_sw, DISP, JAL, JTYPE, Kill, LUI, MEMREAD, REGDEST, RegInputs_regwrite_2, REGWRITE, SIGNEXT,
       YFROMREG;
  wire [1:0] rd, RegInputs_readreg0, RegInputs_readreg1, RegInputs_writereg, rs, rt;
  wire [3:0] AluInputs_switch, funct, opcode;
  wire [7:0] imm8;
  wire [11:0] jaddr;
  wire [15:0] AluInputs_alux, AluInputs_aluy, CurrPC, Imm16, MemDataOut, NewPC, RegData0,
       RegInputs_writedata, SavedPC;

  ControlAndLogic CntrlAnd (
    .opcode(opcode), .rtype(CntrlAnd_rtype), .jal(CntrlAnd_jal), .j(CntrlAnd_j), .jr(CntrlAnd_jr),
    .beq(CntrlAnd_beq), .addi(CntrlAnd_addi), .andi(CntrlAnd_andi), .ori(CntrlAnd_ori), .bne(CntrlAnd_bne),
    .sw(CntrlAnd_sw), .lui(CntrlAnd_lui), .lw(CntrlAnd_lw), .disp(CntrlAnd_disp));
  PCLogic PCLogic (.NewPC(NewPC), .Kill(Kill), .clk(clk), .CurrPC(CurrPC), .NextPC(To_Instr_Mem));
  // Probe on CurrPC
  ControlOrLogic CntrlOr (
    .rtype(CntrlAnd_rtype), .jal(CntrlAnd_jal), .j(CntrlAnd_j), .jr(CntrlAnd_jr), .beq(CntrlAnd_beq),
    .addi(CntrlAnd_addi), .andi(CntrlAnd_andi), .ori(CntrlAnd_ori), .bne(CntrlAnd_bne), .sw(CntrlAnd_sw),
    .lui(CntrlAnd_lui), .lw(CntrlAnd_lw), .disp(CntrlAnd_disp), .YFROMREG(YFROMREG), .JTYPE(JTYPE),
    .SIGNEXT(SIGNEXT), .REGDEST(REGDEST), .REGWRITE(REGWRITE), .MEMREAD(MEMREAD), .MEMWRITE(Data_Mem_Write),
    .LUI_2(LUI), .JAL_2(JAL), .DISP_2(DISP));
  InstructionBuffer InstrBuffer (
    .Instruction(From_Instr_Mem), .KillSwitch(Kill), .clk(clk), .opcode(opcode), .funct(funct), .rs(rs),
    .rt(rt), .rd(rd), .imm8(imm8), .jaddr(jaddr));
  Extender Extender (.imm8(imm8), .SignExtend(SIGNEXT), .imm16(Imm16));
  RegfileInputs RegInputs (
    .rs(rs), .rt(rt), .rd(rd), .AluResult(Data_Mem_Addr), .MemDataOut(MemDataOut), .SavedPC(SavedPC),
    .REGDEST(REGDEST), .REGWRITE(REGWRITE), .MEMREAD(MEMREAD), .JAL(JAL), .ReadReg0(RegInputs_readreg0),
    .ReadReg1(RegInputs_readreg1), .WriteReg(RegInputs_writereg), .WriteData(RegInputs_writedata),
    .RegWrite_2(RegInputs_regwrite_2));
  Regfile_main Regfile (
    .Read_register_1(RegInputs_readreg0), .Read_register_2(RegInputs_readreg1),
    .write_register(RegInputs_writereg), .write_data(RegInputs_writedata), .Reg_0_Value(r0),
    .Reg_1_Value(r1), .Reg_2_Value(r2), .Reg_3_Value(r3), .RegWrite(RegInputs_regwrite_2), .clock(clk),
    .Read_Data_1(RegData0), .Read_Data_2(Data_Mem_Data));
  Jumps_Branches Jumps_Branches (
    .CurrPC(CurrPC), .opcode(opcode), .imm8(imm8), .jaddr(jaddr), .RegData0(RegData0), .AluEqual(AluEqual),
    .JTYPE(JTYPE), .NewPC(NewPC), .SavedPC(SavedPC), .KillSwitch(Kill));
  Hex_Digit_Display hex_digit_display_1 (.value(Display_0[15:12]));  // open: dp
  Hex_Digit_Display hex_digit_display_2 (.value(Display_1[15:12]));  // open: dp
  // Probe on RegData0
  // Probe on Data_Mem_Data
  DataMemory DataMem (
    .Address(Data_Mem_Addr), .DataIn(Data_Mem_Data), .MemWrite(Data_Mem_Write), .CLK(clk),
    .DataOut(MemDataOut));
  Hex_Digit_Display hex_digit_display_3 (.value(Display_0[11:8]));  // open: dp
  Hex_Digit_Display hex_digit_display_4 (.value(Display_0[7:4]));  // open: dp
  Hex_Digit_Display hex_digit_display_5 (.value(Display_1[11:8]));  // open: dp
  Hex_Digit_Display hex_digit_display_6 (.value(Display_1[7:4]));  // open: dp
  Hex_Digit_Display hex_digit_display_7 (.value(Display_0[3:0]));  // open: dp
  Hex_Digit_Display hex_digit_display_8 (.value(Display_1[3:0]));  // open: dp
  OutputDevices OutDev (
    .Input(RegData0), .Display(DISP), .Imm(imm8), .CLK(clk), .Display0(Display_0), .Display1(Display_1));
  AluInputs AluInputs (
    .RegData0(RegData0), .RegData1(Data_Mem_Data), .Imm16(Imm16), .opcode(opcode), .funct(funct),
    .YFROMREG(YFROMREG), .LUI(LUI), .AluX(AluInputs_alux), .AluY(AluInputs_aluy), .Switch(AluInputs_switch));
  alu_main ALU (
    .Switch__S(AluInputs_switch), .X(AluInputs_alux), .Equal(AluEqual), .RESULT(Data_Mem_Addr),
    .Signed_Overflow(AluOverflow), .Y(AluInputs_aluy));
  LED Signed_Overflow (.in(AluOverflow));

  // Other names for the same wires on the sheet: AluResult[15:0] = Data_Mem_Addr; d0[15:0] = Display_0;
  //   d1[15:0] = Display_1; MEMWRITE = Data_Mem_Write; NextPC[15:0] = To_Instr_Mem; RegData1[15:0] = Data_Mem_Data

  // Notes on the sheet:
  //   This is the current PC that you need to send as OUTPUT
  //   This is the instruction that you would receive as INPUT
  //   This is a CLK that is an INPUT driven from the harness.
  //   Remember, this circuit is loaded from the harness to be tested!
  //   DO NOT CHANGE THE LOCATIONS OF THE INPUTS OR OUTPUTS! IF YOU DO SO, YOU NEED TO MAKE SURE THE PINS ARE IN THE RIGHT PLACES!
  //   These are OUTPUTS of the circuit
  //   These are OUTPUTS of the circuit
endmodule

module DataMemory (
  input  [15:0] Address,
  input  [15:0] DataIn,
  input  MemWrite,
  input  CLK,
  output [15:0] DataOut
);

  wire not_1_out;

  not not_1 (not_1_out, MemWrite);
  RAM #(.addrWidth(16), .dataWidth(16), .bus("separate")) ram_1 (
    .addr(Address), .din(DataIn), .data(DataOut), .str(MemWrite), .sel(1'b1), .clk(CLK), .ld(not_1_out));  // open: clr
endmodule

module OutputDevices (
  input  [15:0] Input,
  input  Display,
  input  [7:0] Imm,
  input  CLK,
  output [15:0] Display0,
  output [15:0] Display1
);

  wire bitselector_1_out, demultiplexer_1_out0, demultiplexer_1_out1;

  Demultiplexer #(.enable("false")) demultiplexer_1 (
    .out0(demultiplexer_1_out0), .out1(demultiplexer_1_out1), .in(Display), .sel(bitselector_1_out));
  BitSelector bitselector_1 (.in(Imm), .out(bitselector_1_out), .sel(3'b000));
  Register #(.width(16)) register_1 (.D(Input), .en(demultiplexer_1_out0), .Q(Display0), .clk(CLK));  // open: clr
  Register #(.width(16)) register_2 (.D(Input), .en(demultiplexer_1_out1), .Q(Display1), .clk(CLK));  // open: clr
endmodule

module OpsMap (
  input  [3:0] opcode,
  output [3:0] funct
);

  wire and_1_out, and_2_out, not_1_out, not_2_out, not_3_out;
  wire [0:0] not_4_out;
  wire [3:0] multiplexer_1_out;

  not not_1 (not_1_out, opcode[0]);
  not not_2 (not_2_out, opcode[2]);
  and and_1 (and_1_out, opcode[1], opcode[2], not_3_out);
  not not_3 (not_3_out, opcode[3]);
  and and_2 (and_2_out, not_1_out, opcode[1], not_2_out, opcode[3]);
  Multiplexer #(.width(4)) multiplexer_1 (
    .in0(4'b0000), .in1({opcode[3:1], not_4_out[0]}), .out(multiplexer_1_out), .sel(and_1_out));  // open: en
  not not_4 (not_4_out[0], opcode[0]);
  Multiplexer #(.width(4)) multiplexer_2 (
    .in0(multiplexer_1_out), .in1(4'b0010), .out(funct), .sel(and_2_out));  // open: en
endmodule

module Extender (
  input  [7:0] imm8,
  input  SignExtend,
  output [15:0] imm16
);

  wire and_1_out, bitselector_1_out;

  BitSelector bitselector_1 (.in(imm8), .out(bitselector_1_out), .sel(3'b111));
  Multiplexer #(.width(8)) multiplexer_1 (
    .in0({8{1'b0}}), .in1({8{1'b1}}), .out(imm16[15:8]), .sel(and_1_out));  // open: en
  and and_1 (and_1_out, bitselector_1_out, SignExtend);

  assign imm16[7:0] = imm8;
endmodule

module BranchHandler (
  input  [15:0] CurrPC,
  input  [7:0] BranchOff,
  input  [3:0] opcode,
  input  Equal,
  output [15:0] NewPC,
  output KillNext
);

  wire and_1_out, not_1_out, not_2_out, xor_1_out, xor_2_out;
  wire [15:0] adder_1_out, extender_1_imm16;

  Extender extender_1 (.imm8(BranchOff), .SignExtend(1'b1), .imm16(extender_1_imm16));
  Adder #(.width(16)) adder_1 (.a(16'h1), .b(CurrPC), .out(adder_1_out));  // open: cin, cout
  not not_1 (not_1_out, opcode[0]);
  not not_2 (not_2_out, opcode[1]);
  xor xor_1 (xor_1_out, opcode[2], opcode[3]);
  xor xor_2 (xor_2_out, opcode[3], Equal);
  Adder #(.width(16)) adder_2 (.a(adder_1_out), .b(extender_1_imm16), .out(NewPC));  // open: cin, cout
  and and_1 (and_1_out, not_1_out, not_2_out, xor_1_out);
  and and_2 (KillNext, and_1_out, xor_2_out);
endmodule

module JumpHandler (
  input  [15:0] CurrPC,
  input  [11:0] JumpAddr,
  input  [15:0] DestAddr,
  input  [3:0] opcode,
  output [15:0] SavedPC,
  output [15:0] NewPC,
  output KillNext
);

  wire and_3_out, not_1_out, not_2_out, or_1_out;
  wire [15:0] and_1_out, or_2_out;

  not not_1 (not_1_out, opcode[2]);
  not not_2 (not_2_out, opcode[3]);
  assign and_1_out = CurrPC & 16'hf000;  // AND_Gate and_1, 16 bits wide
  or or_1 (or_1_out, opcode[0], opcode[1]);
  assign or_2_out = and_1_out | {4'b0000, JumpAddr};  // OR_Gate or_2, 16 bits wide
  Multiplexer #(.width(16)) multiplexer_1 (.in0(or_2_out), .in1(DestAddr), .out(NewPC), .sel(and_3_out));  // open: en
  and and_2 (KillNext, or_1_out, not_1_out, not_2_out);
  and and_3 (and_3_out, opcode[0], opcode[1], not_1_out, not_2_out);
  Adder #(.width(16)) adder_1 (.a(CurrPC), .b(16'h1), .out(SavedPC));  // open: cin, cout
endmodule

module PCLogic (
  input  [15:0] NewPC,
  input  Kill,
  input  clk,
  output [15:0] CurrPC,
  output [15:0] NextPC
);

  wire comparator_1_gt, counter_1_q, KillStore_q;
  wire [15:0] adder_1_out, multiplexer_1_out, multiplexer_2_out;

  Multiplexer #(.width(16)) multiplexer_1 (.in0(NextPC), .in1(NewPC), .out(multiplexer_1_out), .sel(Kill));  // open: en
  Register #(.width(16)) StoredPC (.D(multiplexer_1_out), .Q(CurrPC), .clk(clk));  // open: en, clr
  Adder #(.width(16)) adder_1 (.a(CurrPC), .b(16'h1), .out(adder_1_out));  // open: cin, cout
  Counter #(.width(1), .max('h1), .ongoal("stay")) counter_1 (
    .load(1'b0), .count(1'b1), .Q(counter_1_q), .clk(clk));  // open: D, carry, clr
  Multiplexer #(.width(16)) multiplexer_2 (
    .in0({16{1'b0}}), .in1(adder_1_out), .out(multiplexer_2_out), .sel(comparator_1_gt));  // open: en
  Comparator #(.width(1), .mode("unsigned")) comparator_1 (
    .a(counter_1_q), .b(1'b0), .gt(comparator_1_gt));  // open: eq, lt
  Register #(.width(1)) KillStore (.D(Kill), .Q(KillStore_q), .clk(clk));  // open: en, clr
  Multiplexer #(.width(16)) multiplexer_3 (
    .in0(multiplexer_2_out), .in1(CurrPC), .out(NextPC), .sel(KillStore_q));  // open: en
endmodule

module ControlAndLogic (
  input  [3:0] opcode,
  output rtype,
  output jal,
  output j,
  output jr,
  output beq,
  output addi,
  output andi,
  output ori,
  output bne,
  output sw,
  output lui,
  output lw,
  output disp
);

  wire not_1_out, not_2_out, not_3_out, not_4_out;

  not not_1 (not_1_out, opcode[0]);
  not not_2 (not_2_out, opcode[1]);
  not not_3 (not_3_out, opcode[2]);
  not not_4 (not_4_out, opcode[3]);
  and and_1 (rtype, not_1_out, not_2_out, not_3_out, not_4_out);
  and and_2 (jal, opcode[0], not_2_out, not_3_out, not_4_out);
  and and_3 (j, not_1_out, opcode[1], not_3_out, not_4_out);
  and and_4 (jr, opcode[0], opcode[1], not_3_out, not_4_out);
  and and_5 (beq, not_1_out, not_2_out, opcode[2], not_4_out);
  and and_6 (addi, opcode[0], not_2_out, opcode[2], not_4_out);
  and and_7 (andi, not_1_out, opcode[1], opcode[2], not_4_out);
  and and_8 (ori, opcode[0], opcode[1], opcode[2], not_4_out);
  and and_9 (sw, opcode[0], not_2_out, not_3_out, opcode[3]);
  and and_10 (bne, not_1_out, not_2_out, not_3_out, opcode[3]);
  and and_11 (lui, not_1_out, opcode[1], not_3_out, opcode[3]);
  and and_12 (lw, opcode[0], opcode[1], not_3_out, opcode[3]);
  and and_13 (disp, not_1_out, not_2_out, opcode[2], opcode[3]);
endmodule

module ControlOrLogic (
  input  rtype,
  input  jal,
  input  j,
  input  jr,
  input  beq,
  input  addi,
  input  andi,
  input  ori,
  input  bne,
  input  sw,
  input  lui,
  input  lw,
  input  disp,
  output YFROMREG,
  output JTYPE,
  output SIGNEXT,
  output REGDEST,
  output REGWRITE,
  output MEMREAD,
  output MEMWRITE,
  output LUI_2,
  output JAL_2,
  output DISP_2
);

  or or_1 (YFROMREG, bne, beq, rtype);
  or or_2 (JTYPE, jr, j, jal);
  or or_3 (SIGNEXT, lw, sw, addi);
  or or_4 (REGDEST, lw, lui, ori, andi, addi);
  or or_5 (REGWRITE, REGDEST, jal, rtype);

  assign DISP_2 = disp;
  assign JAL_2 = jal;
  assign LUI_2 = lui;
  assign MEMREAD = lw;
  assign MEMWRITE = sw;
endmodule

module RegfileInputs (
  input  [1:0] rs,
  input  [1:0] rt,
  input  [1:0] rd,
  input  [15:0] AluResult,
  input  [15:0] MemDataOut,
  input  [15:0] SavedPC,
  input  REGDEST,
  input  REGWRITE,
  input  MEMREAD,
  input  JAL,
  output [1:0] ReadReg0,
  output [1:0] ReadReg1,
  output [1:0] WriteReg,
  output [15:0] WriteData,
  output RegWrite_2
);

  wire [1:0] multiplexer_1_out;
  wire [15:0] multiplexer_2_out;

  Multiplexer #(.width(2)) multiplexer_1 (.in0(rd), .in1(rt), .out(multiplexer_1_out), .sel(REGDEST));  // open: en
  Multiplexer #(.width(16)) multiplexer_2 (
    .in0(AluResult), .in1(MemDataOut), .out(multiplexer_2_out), .sel(MEMREAD));  // open: en
  Multiplexer #(.width(16)) multiplexer_3 (
    .in0(multiplexer_2_out), .in1(SavedPC), .out(WriteData), .sel(JAL));  // open: en
  Multiplexer #(.width(2)) multiplexer_4 (.in0(multiplexer_1_out), .in1(2'b11), .out(WriteReg), .sel(JAL));  // open: en

  assign ReadReg0 = rs;
  assign ReadReg1 = rt;
  assign RegWrite_2 = REGWRITE;
endmodule

module AluInputs (
  input  [15:0] RegData0,
  input  [15:0] RegData1,
  input  [15:0] Imm16,
  input  [3:0] opcode,
  input  [3:0] funct,
  input  YFROMREG,
  input  LUI,
  output [15:0] AluX,
  output [15:0] AluY,
  output [3:0] Switch
);

  wire [3:0] OpsMap_funct;
  wire [15:0] multiplexer_2_out;

  Multiplexer #(.width(16)) multiplexer_1 (.in0(RegData0), .in1(Imm16), .out(AluX), .sel(LUI));  // open: en
  Multiplexer #(.width(16)) multiplexer_2 (
    .in0(Imm16), .in1(RegData1), .out(multiplexer_2_out), .sel(YFROMREG));  // open: en
  OpsMap OpsMap (.opcode(opcode), .funct(OpsMap_funct));
  Multiplexer #(.width(16)) multiplexer_3 (.in0(multiplexer_2_out), .in1(16'h8), .out(AluY), .sel(LUI));  // open: en
  Multiplexer #(.width(4)) multiplexer_4 (.in0(OpsMap_funct), .in1(funct), .out(Switch), .sel(YFROMREG));  // open: en
endmodule

module InstructionBuffer (
  input  [15:0] Instruction,
  input  KillSwitch,
  input  clk,
  output [3:0] opcode,
  output [3:0] funct,
  output [1:0] rs,
  output [1:0] rt,
  output [1:0] rd,
  output [7:0] imm8,
  output [11:0] jaddr
);

  wire [15:0] multiplexer_1_out;

  Multiplexer #(.width(16)) multiplexer_1 (
    .in0(Instruction), .in1(16'h6), .out(multiplexer_1_out), .sel(KillSwitch));  // open: en
  Register #(.width(16)) Buffer (
    .D(multiplexer_1_out), .Q({opcode, jaddr[11:8], imm8[7:4], funct}), .clk(clk));  // open: en, clr

  assign imm8[3:0] = funct;
  assign jaddr[7:0] = {imm8[7:4], funct};
  assign rd = imm8[7:6];
  assign rs = jaddr[11:10];
  assign rt = jaddr[9:8];
endmodule

module Jumps_Branches (
  input  [15:0] CurrPC,
  input  [3:0] opcode,
  input  [7:0] imm8,
  input  [11:0] jaddr,
  input  [15:0] RegData0,
  input  AluEqual,
  input  JTYPE,
  output [15:0] NewPC,
  output [15:0] SavedPC,
  output KillSwitch
);

  wire Branches_killnext, Jumps_killnext, not_1_out;
  wire [15:0] Branches_newpc, Jumps_newpc;

  JumpHandler Jumps (
    .CurrPC(CurrPC), .JumpAddr(jaddr), .DestAddr(RegData0), .opcode(opcode), .SavedPC(SavedPC),
    .NewPC(Jumps_newpc), .KillNext(Jumps_killnext));
  BranchHandler Branches (
    .CurrPC(CurrPC), .BranchOff(imm8), .opcode(opcode), .Equal(AluEqual), .NewPC(Branches_newpc),
    .KillNext(Branches_killnext));
  Multiplexer #(.width(16)) multiplexer_1 (
    .in0(Jumps_newpc), .in1(Branches_newpc), .out(NewPC), .sel(not_1_out));  // open: en
  not not_1 (not_1_out, JTYPE);
  or or_1 (KillSwitch, Jumps_killnext, Branches_killnext);
endmodule
